// Digital circuit ALU.dig as structural Verilog
module ALU (
  input  En,
  input  [2:0] Op,
  input  [7:0] N,
  input  Clk,
  output [7:0] out_4,
  output [7:0] out_5
);

  wire [7:0] multiplexer_1_out, multiplexer_2_out, N_plus_S, N_S, NAND, Q, R, S, SD, SE, Sub, XOR;

  somador_8_bits somador_8_bits_1 (.AC(out_4), .N(N), .Cin(1'b0), .Soma(S));  // open: Cout
  Subtrator subtrator_1 (.AC(out_4), .N(N), .Cin(1'b1), .Resultado(Sub));  // open: Cout
  Multiplicador_8_bits multiplicador_8_bits_1 (.Ac(out_4), .N(N), .\Saída ({N_plus_S, N_S}));
  Divisor divisor_1 (.Ac(out_4), .N(N), .Resto(R), .Quociente(Q));
  assign NAND = ~(out_4 & N);  // NAnd nand_1, 8 bits wide
  assign XOR = out_4 ^ N;  // XOr xor_1, 8 bits wide
  ShiftEsquerda shiftesquerda_1 (.Ac(out_4), .Saida(SE));
  ShiftDireita shiftdireita_1 (.Ac(out_4), .Saida(SD));
  Multiplexer #(.Selector_Bits(3), .Bits(8)) multiplexer_1 (
    .sel(Op), .in_0(S), .in_1(Sub), .in_2(N_S), .in_3(R), .in_4(NAND), .in_5(XOR), .in_6(SE), .in_7(SD),
    .out(multiplexer_1_out));
  Multiplexer #(.Selector_Bits(3), .Bits(8)) multiplexer_2 (
    .sel(Op), .in_0(out_5), .in_1(out_5), .in_2(N_plus_S), .in_3(Q), .in_4(out_5), .in_5(out_5),
    .in_6(out_5), .in_7(out_5), .out(multiplexer_2_out));
  Register #(.Bits(8)) Registrador_AC (.D(multiplexer_1_out), .C(Clk), .en(En), .Q(out_4));
  Register #(.Bits(8)) Registrador_MQ (.D(multiplexer_2_out), .C(Clk), .en(En), .Q(out_5));

  // Other names for the same wires on the sheet: AC[7:0] = out_4; MQ[7:0] = out_5
endmodule
