// Digital circuit CPU.dig as structural Verilog
module CPU (
  input  En,
  input  Clk,
  output [7:0] AC,
  output [7:0] MQ
);

  wire [2:0] OP;
  wire [7:0] N, S;

  Counter #(.Bits(8)) counter_1 (.en(En), .C(Clk), .clr(1'b0), .out(S));  // open: ovf
  ROM #(.AddrBits(8), .Bits(11)) rom_1 (.A(S), .sel(1'b1), .D({N, OP}));
  ALU alu_1 (.En(En), .Op(OP), .N(N), .Clk(Clk));

  // Notes on the sheet:
  //   contents of rom_1 (hex, n*v repeats v):
  //   28,2a,50,a1
endmodule
