// Digital circuit Divisor.dig as structural Verilog
module Divisor (
  input  [7:0] Ac,
  input  [7:0] N,
  output [7:0] Resto,
  output [7:0] Quociente
);

  wire [7:0] R0, R1, R2, R3, R4, R5, R6;

  celula_div celula_div_1 (.R1({8{1'b0}}), .N(N), .AC(Ac[7]), .R2(R0), .Quociente(Quociente[7]));
  celula_div celula_div_2 (.R1(R0), .N(N), .AC(Ac[6]), .R2(R1), .Quociente(Quociente[6]));
  celula_div celula_div_3 (.R1(R1), .N(N), .AC(Ac[5]), .R2(R2), .Quociente(Quociente[5]));
  celula_div celula_div_4 (.R1(R2), .N(N), .AC(Ac[4]), .R2(R3), .Quociente(Quociente[4]));
  celula_div celula_div_5 (.R1(R3), .N(N), .AC(Ac[3]), .R2(R4), .Quociente(Quociente[3]));
  celula_div celula_div_6 (.R1(R4), .N(N), .AC(Ac[2]), .R2(R5), .Quociente(Quociente[2]));
  celula_div celula_div_7 (.R1(R5), .N(N), .AC(Ac[1]), .R2(R6), .Quociente(Quociente[1]));
  celula_div celula_div_8 (.R1(R6), .N(N), .AC(Ac[0]), .R2(Resto), .Quociente(Quociente[0]));

  // Other names for the same wires on the sheet: Q0 = Quociente[7]; Q1 = Quociente[6]; Q2 = Quociente[5];
  //   Q3 = Quociente[4]; Q4 = Quociente[3]; Q5 = Quociente[2]; Q6 = Quociente[1]; Q7 = Quociente[0]; R7[7:0] = Resto
endmodule
