// Digital circuit Multiplicador 8 bits.dig as structural Verilog
module Multiplicador_8_bits (
  input  [7:0] Ac,
  input  [7:0] N,
  output [15:0] \Saída 
);

  wire somador_8_bits_1_cout, somador_8_bits_2_cout, somador_8_bits_3_cout, somador_8_bits_4_cout,
       somador_8_bits_5_cout, somador_8_bits_6_cout, somador_8_bits_8_cout;
  wire [0:0] and_16_out;
  wire [1:0] and_24_out;
  wire [2:0] and_32_out;
  wire [3:0] and_40_out;
  wire [4:0] and_48_out;
  wire [5:0] and_56_out;
  wire [6:0] and_64_out;
  wire [7:0] and_8_out, somador_8_bits_2_soma, somador_8_bits_3_soma, somador_8_bits_4_soma,
       somador_8_bits_5_soma, somador_8_bits_6_soma, somador_8_bits_8_soma, somador_8_bits_9_soma,
       somador_8_bits_10_soma, somador_8_bits_11_soma, somador_8_bits_12_soma, somador_8_bits_13_soma,
       somador_8_bits_14_soma;
  wire [7:1] and_15_out;
  wire [7:2] and_22_out;
  wire [7:3] and_29_out;
  wire [7:4] and_36_out;
  wire [7:5] and_43_out;
  wire [7:6] and_50_out;
  wire [7:7] and_57_out;

  and and_1 (and_8_out[0], Ac[0], N[0]);
  and and_2 (and_8_out[1], Ac[1], N[0]);
  and and_3 (and_8_out[2], Ac[2], N[0]);
  and and_4 (and_8_out[3], Ac[3], N[0]);
  and and_5 (and_8_out[4], Ac[4], N[0]);
  and and_6 (and_8_out[5], Ac[5], N[0]);
  and and_7 (and_8_out[6], Ac[6], N[0]);
  and and_8 (and_8_out[7], Ac[7], N[0]);
  and and_9 (and_15_out[1], Ac[0], N[1]);
  and and_10 (and_15_out[2], Ac[1], N[1]);
  and and_11 (and_15_out[3], Ac[2], N[1]);
  and and_12 (and_15_out[4], Ac[3], N[1]);
  and and_13 (and_15_out[5], Ac[4], N[1]);
  and and_14 (and_15_out[6], Ac[5], N[1]);
  and and_15 (and_15_out[7], Ac[6], N[1]);
  and and_16 (and_16_out[0], Ac[7], N[1]);
  and and_17 (and_22_out[2], Ac[0], N[2]);
  and and_18 (and_22_out[3], Ac[1], N[2]);
  and and_19 (and_22_out[4], Ac[2], N[2]);
  and and_20 (and_22_out[5], Ac[3], N[2]);
  and and_21 (and_22_out[6], Ac[4], N[2]);
  and and_22 (and_22_out[7], Ac[5], N[2]);
  and and_23 (and_24_out[0], Ac[6], N[2]);
  and and_24 (and_24_out[1], Ac[7], N[2]);
  and and_25 (and_29_out[3], Ac[0], N[3]);
  and and_26 (and_29_out[4], Ac[1], N[3]);
  and and_27 (and_29_out[5], Ac[2], N[3]);
  and and_28 (and_29_out[6], Ac[3], N[3]);
  and and_29 (and_29_out[7], Ac[4], N[3]);
  and and_30 (and_32_out[0], Ac[5], N[3]);
  and and_31 (and_32_out[1], Ac[6], N[3]);
  and and_32 (and_32_out[2], Ac[7], N[3]);
  and and_33 (and_36_out[4], Ac[0], N[4]);
  and and_34 (and_36_out[5], Ac[1], N[4]);
  and and_35 (and_36_out[6], Ac[2], N[4]);
  and and_36 (and_36_out[7], Ac[3], N[4]);
  and and_37 (and_40_out[0], Ac[4], N[4]);
  and and_38 (and_40_out[1], Ac[5], N[4]);
  and and_39 (and_40_out[2], Ac[6], N[4]);
  and and_40 (and_40_out[3], Ac[7], N[4]);
  and and_41 (and_43_out[5], Ac[0], N[5]);
  and and_42 (and_43_out[6], Ac[1], N[5]);
  and and_43 (and_43_out[7], Ac[2], N[5]);
  and and_44 (and_48_out[0], Ac[3], N[5]);
  and and_45 (and_48_out[1], Ac[4], N[5]);
  and and_46 (and_48_out[2], Ac[5], N[5]);
  and and_47 (and_48_out[3], Ac[6], N[5]);
  and and_48 (and_48_out[4], Ac[7], N[5]);
  and and_49 (and_50_out[6], Ac[0], N[6]);
  and and_50 (and_50_out[7], Ac[1], N[6]);
  and and_51 (and_56_out[0], Ac[2], N[6]);
  and and_52 (and_56_out[1], Ac[3], N[6]);
  and and_53 (and_56_out[2], Ac[4], N[6]);
  and and_54 (and_56_out[3], Ac[5], N[6]);
  and and_55 (and_56_out[4], Ac[6], N[6]);
  and and_56 (and_56_out[5], Ac[7], N[6]);
  and and_57 (and_57_out[7], Ac[0], N[7]);
  and and_58 (and_64_out[0], Ac[1], N[7]);
  and and_59 (and_64_out[1], Ac[2], N[7]);
  and and_60 (and_64_out[2], Ac[3], N[7]);
  and and_61 (and_64_out[3], Ac[4], N[7]);
  and and_62 (and_64_out[4], Ac[5], N[7]);
  and and_63 (and_64_out[5], Ac[6], N[7]);
  and and_64 (and_64_out[6], Ac[7], N[7]);
  somador_8_bits somador_8_bits_1 (
    .AC(somador_8_bits_3_soma), .N({and_57_out[7], {7{1'b0}}}), .Cin(1'b0), .Soma(\Saída [7:0]),
    .Cout(somador_8_bits_1_cout));
  somador_8_bits somador_8_bits_2 (
    .AC(somador_8_bits_5_soma), .N({and_43_out, {5{1'b0}}}), .Cin(1'b0), .Soma(somador_8_bits_2_soma),
    .Cout(somador_8_bits_2_cout));
  somador_8_bits somador_8_bits_3 (
    .AC(somador_8_bits_2_soma), .N({and_50_out, {6{1'b0}}}), .Cin(1'b0), .Soma(somador_8_bits_3_soma),
    .Cout(somador_8_bits_3_cout));
  somador_8_bits somador_8_bits_4 (
    .AC(somador_8_bits_6_soma), .N({and_29_out, 3'b000}), .Cin(1'b0), .Soma(somador_8_bits_4_soma),
    .Cout(somador_8_bits_4_cout));
  somador_8_bits somador_8_bits_5 (
    .AC(somador_8_bits_4_soma), .N({and_36_out, 4'b0000}), .Cin(1'b0), .Soma(somador_8_bits_5_soma),
    .Cout(somador_8_bits_5_cout));
  somador_8_bits somador_8_bits_6 (
    .AC(somador_8_bits_8_soma), .N({and_22_out, 2'b00}), .Cin(1'b0), .Soma(somador_8_bits_6_soma),
    .Cout(somador_8_bits_6_cout));
  somador_8_bits somador_8_bits_7 (
    .AC(somador_8_bits_9_soma), .N({1'b0, and_64_out}), .Cin(somador_8_bits_1_cout), .Soma(\Saída [15:8]));  // open: Cout
  somador_8_bits somador_8_bits_8 (
    .AC(and_8_out), .N({and_15_out, 1'b0}), .Cin(1'b0), .Soma(somador_8_bits_8_soma),
    .Cout(somador_8_bits_8_cout));
  somador_8_bits somador_8_bits_9 (
    .AC(somador_8_bits_11_soma), .N({2'b00, and_56_out}), .Cin(somador_8_bits_3_cout),
    .Soma(somador_8_bits_9_soma));  // open: Cout
  somador_8_bits somador_8_bits_10 (
    .AC(somador_8_bits_12_soma), .N({4'b0000, and_40_out}), .Cin(somador_8_bits_5_cout),
    .Soma(somador_8_bits_10_soma));  // open: Cout
  somador_8_bits somador_8_bits_11 (
    .AC(somador_8_bits_10_soma), .N({3'b000, and_48_out}), .Cin(somador_8_bits_2_cout),
    .Soma(somador_8_bits_11_soma));  // open: Cout
  somador_8_bits somador_8_bits_12 (
    .AC(somador_8_bits_13_soma), .N({{5{1'b0}}, and_32_out}), .Cin(somador_8_bits_4_cout),
    .Soma(somador_8_bits_12_soma));  // open: Cout
  somador_8_bits somador_8_bits_13 (
    .AC(somador_8_bits_14_soma), .N({{6{1'b0}}, and_24_out}), .Cin(somador_8_bits_6_cout),
    .Soma(somador_8_bits_13_soma));  // open: Cout
  somador_8_bits somador_8_bits_14 (
    .AC({8{1'b0}}), .N({{7{1'b0}}, and_16_out[0]}), .Cin(somador_8_bits_8_cout), .Soma(somador_8_bits_14_soma));  // open: Cout
endmodule
