// Digital circuit Subtrator.dig as structural Verilog
module Subtrator (
  input  [7:0] AC,
  input  [7:0] N,
  input  Cin,
  output [7:0] Resultado,
  output Cout
);

  wire Cout0, Cout1, Cout2, Cout3, Cout4, Cout5, Cout6, N0, N1, N2, N3, N4, N5, N6, N7;

  assign {N7, N6, N5, N4, N3, N2, N1, N0} = ~N;  // Not not_1, 8 bits wide
  // Somador somador_1: pin names not known; wires that end beside it: AC[0], N0, Cin, Cout0, Resultado[0]
  // Somador somador_2: pin names not known; wires that end beside it: AC[1], N1, Cout0, Cout1, Resultado[1]
  // Somador somador_3: pin names not known; wires that end beside it: AC[2], N2, Cout1, Cout2, Resultado[2]
  // Somador somador_4: pin names not known; wires that end beside it: AC[3], N3, Cout2, Cout3, Resultado[3]
  // Somador somador_5: pin names not known; wires that end beside it: AC[4], N4, Cout3, Cout4, Resultado[4]
  // Somador somador_6: pin names not known; wires that end beside it: AC[5], N5, Cout4, Cout5, Resultado[5]
  // Somador somador_7: pin names not known; wires that end beside it: AC[6], N6, Cout5, Cout6, Resultado[6]
  // Somador somador_8: pin names not known; wires that end beside it: AC[7], N7, Cout6, Cout, Resultado[7]

  // Other names for the same wires on the sheet: Cout7 = Cout; Soma0 = Resultado[0]; Soma1 = Resultado[1];
  //   Soma2 = Resultado[2]; Soma3 = Resultado[3]; Soma4 = Resultado[4]; Soma5 = Resultado[5]; Soma6 = Resultado[6];
  //   Soma7 = Resultado[7]

  // Notes on the sheet:
  //   Cin: default 1
endmodule
