// Digital circuit celula_div.dig as structural Verilog
module celula_div (
  input  [7:0] R1,
  input  [7:0] N,
  input  AC,
  output [7:0] R2,
  output Quociente
);

  wire [7:0] Resultado;

  Subtrator subtrator_1 (.AC({R1[6:0], AC}), .N(N), .Cin(1'b1), .Resultado(Resultado), .Cout(Quociente));
  Multiplexer #(.Bits(8)) multiplexer_1 (.sel(Quociente), .in_0({R1[6:0], AC}), .in_1(Resultado), .out(R2));

  // Other names for the same wires on the sheet: A[7:0] = {R1[6:0], AC}; Cout = Quociente; MTPX[7:0] = R2
endmodule
