// Digital circuit somador 8 bits.dig as structural Verilog
module somador_8_bits (
  input  [7:0] AC,
  input  [7:0] N,
  input  Cin,
  output [7:0] Soma,
  output Cout
);

  wire Cout0, Cout1, Cout2, Cout3, Cout4, Cout5, Cout6;

  // Somador somador_1: pin names not known; wires that end beside it: AC[0], N[0], Cin, Cout0, Soma[0]
  // Somador somador_2: pin names not known; wires that end beside it: AC[1], N[1], Cout0, Cout1, Soma[1]
  // Somador somador_3: pin names not known; wires that end beside it: AC[2], N[2], Cout1, Cout2, Soma[2]
  // Somador somador_4: pin names not known; wires that end beside it: AC[3], N[3], Cout2, Cout3, Soma[3]
  // Somador somador_5: pin names not known; wires that end beside it: AC[4], N[4], Cout3, Cout4, Soma[4]
  // Somador somador_6: pin names not known; wires that end beside it: AC[5], N[5], Cout4, Cout5, Soma[5]
  // Somador somador_7: pin names not known; wires that end beside it: AC[6], N[6], Cout5, Cout6, Soma[6]
  // Somador somador_8: pin names not known; wires that end beside it: AC[7], N[7], Cout6, Cout, Soma[7]

  // Other names for the same wires on the sheet: Cout7 = Cout
endmodule
